// Logisim project somador.circ as structural Verilog: 2 circuits, main circuit main
module main (
  input  [7:0] A,
  input  [7:0] B,
  input  OP,
  output overflow__sem_sinal,
  output overflow__com_sinal,
  output [7:0] R
);

  somador somador ();  // open: c0, A, B, S, c7, c8

  // Notes on the sheet:
  //   José Eduardo
  //   João Seckler, 4603521, joaoseckler@gmail.com
  //   Parte 1: Circuito Somador
  //   Circuito para adição e subtração de números de 8 bits
endmodule

module somador (
  input  [7:0] A,
  input  [7:0] B,
  input  c0,
  output c7,
  output c8,
  output [7:0] S
);
endmodule
